# Fritzing sketch Fishbot_recv1 (saved by Fritzing 0.9.3b)

parts:
  Arduino_Nano = Arduino Nano (Rev3.0)
  U1 = LIPO-1000mAh [package=lipo-1000]
  U2 = LIPO-1000mAh [package=lipo-1000]
  Reed_Switch = Reed switch [package=THT]
  Right_Pectoral_Fin_(Micro_Servo) = Basic Servo
  Tail = Basic Servo
  Middle_Body = Basic Servo
  Left_Pectoral_Fin_(Micro_Servo) = Basic Servo
  LM2596_Buck_Converter = RioRand LM2596
  NRF24L01 = NRF24L01+ Breakout Board
  C1 = Electrolytic Capacitor [capacitance=10µF package="100 mil [THT, electrolytic]"]
  C2 = Ceramic Capacitor [capacitance=100nF package="100 mil [THT, multilayer]"]

nets:
  GND: Arduino_Nano.GND, U2.-, LM2596_Buck_Converter.Pin_1, LM2596_Buck_Converter.Pin_3, NRF24L01.GND, C1.-, C2.1
  N1: Arduino_Nano.D4, Left_Pectoral_Fin_(Micro_Servo).pulse
  N2: Arduino_Nano.D5, Middle_Body.pulse
  N3: Arduino_Nano.D6, Tail.pulse
  N4: Arduino_Nano.D7, Right_Pectoral_Fin_(Micro_Servo).pulse
  N5: Arduino_Nano.D9, NRF24L01.CE
  N6: Arduino_Nano.D10, NRF24L01.CS
  N7: Arduino_Nano.D11/MOSI, NRF24L01.MOSI
  N8: Arduino_Nano.D12/MISO, NRF24L01.MISO
  N9: Arduino_Nano.VIN, Reed_Switch.pin_2, LM2596_Buck_Converter.Pin_0
  3V3: Arduino_Nano.3V3, NRF24L01.VCC, C1.+, C2.0
  N10: Arduino_Nano.D13/SCK, NRF24L01.SCK
  N11: U1.+, Reed_Switch.pin_1
  N12: U1.-, U2.+
  GND_2: Right_Pectoral_Fin_(Micro_Servo).gnd, Tail.gnd, Middle_Body.gnd, Left_Pectoral_Fin_(Micro_Servo).gnd
  N13: Right_Pectoral_Fin_(Micro_Servo).vcc, LM2596_Buck_Converter.Pin_2
  VCC: Tail.vcc, Middle_Body.vcc, Left_Pectoral_Fin_(Micro_Servo).vcc
