# Fritzing sketch Fishbot_trans1 (saved by Fritzing 0.9.3b)

parts:
  Arduino_Nano = Arduino Nano (Rev3.0)
  NRF24L01 = NRF24L01+ Breakout Board
  C3 = Electrolytic Capacitor [capacitance=10µF package="100 mil [THT, electrolytic]"]
  C4 = Ceramic Capacitor [capacitance=100nF package="100 mil [THT, multilayer]"]
  VCC1 = 4 x AAA Battery Mount
  Joystick = Thumb Joystick
  SPST_Switch = SWITCH_SPDT [package=kps-1290]

nets:
  GND: Arduino_Nano.GND, NRF24L01.GND, C3.-, C4.1, VCC1.-, Joystick.GND
  N1: Arduino_Nano.D2, Joystick.SEL
  N2: Arduino_Nano.D9, NRF24L01.CE
  N3: Arduino_Nano.D10, NRF24L01.CS
  N4: Arduino_Nano.D11/MOSI, NRF24L01.MOSI
  N5: Arduino_Nano.D12/MISO, NRF24L01.MISO
  N6: Arduino_Nano.VIN, SPST_Switch.S
  5V: Arduino_Nano.5V, Joystick.VCC
  N7: Arduino_Nano.A1, Joystick.VERT
  N8: Arduino_Nano.A0, Joystick.HORZ
  3V3: Arduino_Nano.3V3, NRF24L01.VCC, C3.+, C4.0
  N9: Arduino_Nano.D13/SCK, NRF24L01.SCK
  N10: VCC1.+, SPST_Switch.P
